# Fritzing sketch robot mk0 - rev1 (saved by Fritzing 0.9.2b)
circuit board: 7.02607cm x 5.59202cm
breadboards: 1

parts:
  J2 = Basic Servo
  J7 = female pin header, 4 pins [form="♀ (female)"]
  J8 = female pin header, 5 pins [form="♀ (female)"]
  U2 = USB+SHIELD [package=usb-b-pth]
  J3 = Basic Servo
  J9 = Basic Servo
  J10 = Basic Servo
  U3 = ESP8266 WiFi Module [part_number=ESP8266]
  R1 = Resistor [tolerance=±5% resistance=10k package=THT]
  R2 = Resistor [tolerance=±5% resistance=10k package=THT]
  R3 = Resistor [tolerance=±5% resistance=10k package=THT]
  U1 = Arduino Uno (Rev3)
  J13 = male pin header, 3 pins [form="♂ (male)"]

nets:
  GND: J2.gnd, J7.pin2, J8.pin4, U2.GND, J3.gnd, J9.gnd, J10.gnd, U3.GND, R3.Pin_1, U1.GND
  VCC: J2.vcc, J3.vcc, J9.vcc, J10.vcc, J13.pin2
  N1: J2.pulse, U1.D10_PWM/SS
  VCC_2: J7.pin1, U3.VCC, R1.Pin_0, U1.3V3
  N2: J7.pin3, U1.D2
  N3: J7.pin4, U1.D3_PWM
  N4: J8.pin1, U1.D11_PWM/MOSI
  N5: J8.pin2, U1.D12/MISO
  N6: J8.pin3, U1.D13/SCK
  N7: J8.pin5, U1.5V, J13.pin3
  N8: U2.VBUS, J13.pin1
  N9: J3.pulse, U1.D9_PWM
  N10: J9.pulse, U1.D8
  N11: J10.pulse, U1.D7
  N12: U3.RXD, R2.Pin_1, R3.Pin_0
  N13: U3.CH_PD, R1.Pin_1
  N14: U3.TXD, U1.D5_PWM
  N15: R2.Pin_0, U1.D4

notes:
  RX
  TX
  GND
  Vcc
  HC-06
  CLK
  CS
  DIN
  MATRIZ
  Bat
  VCC
  SIG
  Ard
  CH_PD
  3V3
  Gnd
  Din
  Clk
  Cs
  Matriz de LEDs
  ESP8266
  Robô da Alegria v1.0
  Por: Igor Fonseca Albuquerque

custom parts:
  ESP8266 WiFi Module: Generic WiFi Module based on the ESP8266 with onboard PCB antenna and UART communications
