# Fritzing sketch robot mk0 - rev6-1 (saved by Fritzing 0.9.2b)
circuit board: 6.98138cm x 6.59903cm
breadboards: 1

parts:
  J1 = Basic Servo
  J7 = female pin header, 4 pins [form="♀ (female)"]
  J6 = female pin header, 5 pins [form="♀ (female)"]
  J2 = Basic Servo
  J3 = Basic Servo
  J8 = ESP8266 WiFi Module [part_number=ESP8266]
  R1 = Resistor [tolerance=±5% resistance=10k package=THT]
  R2 = Resistor [tolerance=±5% resistance=10k package=THT]
  R3 = Resistor [tolerance=±5% resistance=10k package=THT]
  U1 = Arduino Uno (Rev3)
  J13 = male pin header, 3 pins [form="♂ (male)"]
  J4 = Basic Servo
  S1 = Momentary Switch [package=ksa_sealed_tac_switch]
  J17 = male pin header, 3 pins [form="♂ (male)"]
  J16 = male pin header, 3 pins [form="♂ (male)"]
  J11 = male pin header, 2 pins [form="♂ (male)"]
  J5 = Basic Servo
  J12 = male pin header, 2 pins [form="♂ (male)"]
  R4 = Resistor [tolerance=±5% resistance=220 package=THT]
  R5 = Resistor [tolerance=±5% resistance=220 package=THT]
  R6 = Resistor [tolerance=±5% resistance=220 package=THT]
  R7 = Resistor [tolerance=±5% resistance=220 package=THT]
  R8 = Resistor [tolerance=±5% resistance=220 package=THT]
  R9 = Resistor [tolerance=±5% resistance=220 package=THT]
  J18 = male pin header, 3 pins [form="♂ (male)"]
  J15 = male pin header, 4 pins [form="♂ (male)"]
  M4 = DC Motor
  M2 = DC Motor
  M3 = DC Motor
  J9 = L9110 H-bridge module [part_number="L9110 H-bridge"]
  J10 = L9110 H-bridge module [part_number="L9110 H-bridge"]
  M1 = DC Motor

nets:
  GND: J1.gnd, J7.pin2, J6.pin4, J2.gnd, J3.gnd, J8.GND, R3.Pin_1, U1.GND, J4.gnd, S1.1, S1.2, J17.pin1, J17.pin2, J17.pin3, J5.gnd, R7.Pin_0, R8.Pin_0, R9.Pin_0, J15.pin4, J9.GND, J10.GND
  VCC: J1.vcc, J2.vcc, J3.vcc, J13.pin2, J4.vcc, J5.vcc
  N1: J1.pulse, U1.D8
  3.3V: J7.pin1, J8.VCC, R1.Pin_0, U1.3V3
  N2: J7.pin3, J8.TXD, J11.pin2
  N3: J7.pin4, R2.Pin_0, U1.D1/TX
  N4: J6.pin1, U1.D11_PWM/MOSI
  N5: J6.pin2, U1.D12/MISO
  N6: J6.pin3, U1.D13/SCK
  5V: J6.pin5, U1.5V, J13.pin3, J16.pin1, J16.pin2, J16.pin3
  N7: J2.pulse, U1.D7
  N8: J3.pulse, U1.D4
  N9: J8.RXD, R2.Pin_1, R3.Pin_0
  N10: J8.CH_PD, R1.Pin_1
  N11: U1.A0, R6.Pin_0, R9.Pin_1
  N12: U1.A1, R5.Pin_0, R8.Pin_1
  N13: U1.A2, R4.Pin_0, R7.Pin_1
  N14: U1.A3, J18.pin1
  N15: U1.A4/SDA, J18.pin2
  N16: U1.A5/SCL, J18.pin3
  N17: U1.D9_PWM, J9.B-IB, J10.B-IB
  N18: U1.D10_PWM/SS, J9.B-IA, J10.B-IA
  N19: U1.D0/RX, J11.pin1
  N20: U1.D2, J5.pulse
  N21: U1.D3_PWM, J4.pulse
  N22: U1.D5_PWM, J9.A-IB, J10.A-IB
  N23: U1.D6_PWM, J9.A-IA, J10.A-IA
  N24: U1.RESET, S1.3, S1.4
  N25: U1.VIN, J12.pin1
  6V: J13.pin1, R5.Pin_1, J15.pin2, J9.VCC, J10.VCC
  9V: J12.pin2, R4.Pin_1, J15.pin1
  N26: R6.Pin_1, J15.pin3
  N27: M4.pin_1, J9.MOTOR_B-B
  N28: M4.pin_2, J9.MOTOR_B-A
  N29: M2.pin_1, J10.MOTOR_A-B
  N30: M2.pin_2, J10.MOTOR_A-A
  N31: M3.pin_1, J9.MOTOR_A-B
  N32: M3.pin_2, J9.MOTOR_A-A
  N33: J10.MOTOR_B-A, M1.pin_2
  N34: J10.MOTOR_B-B, M1.pin_1

notes:
  RX
  TX
  GND
  Vcc
  HC-06
  CLK
  CS
  DIN
  MATRIZ
  +6V
  +5V
  VCC
  SIG
  CH
  3V3
  Gnd
  Din
  Clk
  Cs
  Matriz de LEDs
  Bat
  Ard
  ESP8266
  Robô da Alegria v2.0
  Por: Igor Fonseca Albuquerque
  reset button
  RESET
  entradas/saídas extras
  progr
  bat
  gnd
  Robô da Alegria, Shield para Arduino Uno do Robô da Alegria, 2
  J1...J5 - Servomotores
  J6 - Matriz de LEDs
  J7 - HC06
  J8 - ESP8266
  J11 - Programacao - Remover jumper antes de fazer upload
  J12 - Alimentacao - Colocar jumper para alimentar Arduino por baterias
  J13 - Alimentacao - Selecionar alimentacao servomotores (Arduino ou baterias)
  J15 - Entrada das baterias (+9V, +6V, +3V, GND)
  J16 - +5V (Arduino)
  J17 - GND
  J18 - Entradas e saidas reservas
  BAT
  +9V
  +3V
  J9 - Motores
  J10 - Motores
  A-IA
  A-IB
  B-IB
  B-IA

custom parts:
  ESP8266 WiFi Module: Generic WiFi Module based on the ESP8266 with onboard PCB antenna and UART communications
