# Fritzing sketch robot mk0 - rev7 (saved by Fritzing 0.9.2b)
breadboards: 1

parts:
  U1 = Arduino Uno (Rev3)
  U3 = 16-Channel 12-bit PWM Servo Driver - I2C [part_number=815]
  U2 = ESP8266 WiFi Module [part_number=ESP8266]
  J2 = Basic Servo
  J3 = Basic Servo
  J4 = Basic Servo
  J1 = Basic Servo
  J6 = Basic Servo
  J5 = Basic Servo
  8x8_LED_Module = 8x8 LED Modul mit MAX7219 [part_number=Boca package=THT]
  8x8_LED_Module_2 = 8x8 LED Modul mit MAX7219 [part_number="Olho esquerdo" package=THT]
  8x8_LED_Module_3 = 8x8 LED Modul mit MAX7219 [part_number="Olho direito" package=THT]
  8x8_LED_Module_4 = 8x8 LED Modul mit MAX7219 [part_number=Boca package=THT]
  BATT1 = 4xAA Switchable Battery Pack w/Bare Wire
  R2 = Resistor [tolerance=±5% resistance=10k package=THT]
  R3 = Resistor [tolerance=±5% resistance=10k package=THT]
  R4 = Resistor [tolerance=±5% resistance=10k package=THT]
  U4 = L9110 H-bridge module [part_number="L9110 H-bridge"]  # not connected

nets:
  N1: U1.A4/SDA, U3.SDA
  N2: U1.A5/SCL, U3.SCL
  N3: U1.D9_PWM, 8x8_LED_Module_4.DIN_Eingang
  N4: U1.D10_PWM/SS, 8x8_LED_Module_4.CS_Eingang
  N5: U1.D11_PWM/MOSI, 8x8_LED_Module_4.CLK_Eingang
  GND: U1.GND, U3.GND, U2.GND, J2.gnd, J3.gnd, J4.gnd, J1.gnd, J6.gnd, J5.gnd, 8x8_LED_Module_4.GND_Eingang, BATT1.NEG, R4.Pin_1
  N6: U1.D4, R2.Pin_0
  N7: U1.D5_PWM, U2.TXD
  3V3: U1.3V3, U2.VCC, R3.Pin_0
  5V: U1.5V, U3.VCC, 8x8_LED_Module_4.VCC_Eingang
  N8: U3.PWRIN, BATT1.POS
  N9: U3.PWM5, J6.pulse
  5V_2: U3.5.0V, J2.vcc, J3.vcc, J4.vcc, J1.vcc, J6.vcc, J5.vcc
  N10: U3.PWM4, J5.pulse
  N11: U3.PWM3, J4.pulse
  N12: U3.PWM2, J3.pulse
  N13: U3.PWM1, J2.pulse
  N14: U3.PWM0, J1.pulse
  N15: U2.RXD, R2.Pin_1, R4.Pin_0
  N16: U2.CH_PD, R3.Pin_1
  N17: 8x8_LED_Module.VCC_Eingang, 8x8_LED_Module_2.VCC_Ausgang
  N18: 8x8_LED_Module.GND_Eingang, 8x8_LED_Module_2.GND_Ausgang
  N19: 8x8_LED_Module.DIN_Eingang, 8x8_LED_Module_2.DOUT_Ausgang
  N20: 8x8_LED_Module.CS_Eingang, 8x8_LED_Module_2.CS_Ausgang
  N21: 8x8_LED_Module.CLK_Eingang, 8x8_LED_Module_2.CLK_Ausgang
  N22: 8x8_LED_Module_2.VCC_Eingang, 8x8_LED_Module_3.VCC_Ausgang
  N23: 8x8_LED_Module_2.GND_Eingang, 8x8_LED_Module_3.GND_Ausgang
  N24: 8x8_LED_Module_2.DIN_Eingang, 8x8_LED_Module_3.DOUT_Ausgang
  N25: 8x8_LED_Module_2.CS_Eingang, 8x8_LED_Module_3.CS_Ausgang
  N26: 8x8_LED_Module_2.CLK_Eingang, 8x8_LED_Module_3.CLK_Ausgang
  N27: 8x8_LED_Module_3.VCC_Eingang, 8x8_LED_Module_4.VCC_Ausgang
  N28: 8x8_LED_Module_3.GND_Eingang, 8x8_LED_Module_4.GND_Ausgang
  N29: 8x8_LED_Module_3.DIN_Eingang, 8x8_LED_Module_4.DOUT_Ausgang
  N30: 8x8_LED_Module_3.CS_Eingang, 8x8_LED_Module_4.CS_Ausgang
  N31: 8x8_LED_Module_3.CLK_Eingang, 8x8_LED_Module_4.CLK_Ausgang

notes:
  Robô da Alegria, Eletrônica, 3
  Por: Igor Fonseca Albuquerque
  Robô da Alegria v3.0
  Boca
  Olho direito
  Olho esquerdo
  Braço esquerdo
  Braço direito
  Pescoço

custom parts:
  16-Channel 12-bit PWM Servo Driver - I2C: You want to make a cool robot, maybe a hexapod walker, or maybe just a piece of art with a lot of moving parts. Or maybe you want to drive a lot of LEDs with precise PWM output. Using only two pins, control 16 free-running PWM outputs! You can even chain up 62 breakouts to control up to 992 PWM outputs.
  ESP8266 WiFi Module: Generic WiFi Module based on the ESP8266 with onboard PCB antenna and UART communications
  4xAA Switchable Battery Pack w/Bare Wire: 4xAA Switchable Battery Pack with Bare Wire connection
